// Logisim project CPU.circ as structural Verilog: 5 circuits, main circuit ALU
module main (
  input  in_1
);

  wire and_1_out, and_2_out, and_3_out, CLK, controlunit_1_bus_buffer_alu, controlunit_1_bus_buffer_iw,
       controlunit_1_bus_register_feedback, controlunit_1_enable_input, controlunit_1_enable_ir,
       controlunit_1_enable_port_a, controlunit_1_enable_port_b, controlunit_1_increment_pc,
       controlunit_1_rom_load_enable, controlunit_1_roml_h, decoder_1_out0, decoder_1_out1, decoder_1_out2,
       decoder_1_out3, decoder_1_out4, decoder_1_out6, Exe, LD, Mem, RAM_IO, RelConst, ST, write;
  wire [0:0] keyboard_1_avail;
  wire [2:0] controlunit_1_port_a_select, controlunit_1_port_b_select, controlunit_1_writeregselect;
  wire [3:0] controlunit_1_alu_cmd;
  wire [6:0] keyboard_1_data, RamAddr, random_1_out;
  wire [7:0] alu_1_res, controlled_buffer_1_out, Flags, multiplexer_1_out, multiplexer_2_out,
       multiplexer_3_out, register_2_pc, RelJ, rom_1_data, rom_1_data_2, RomAddr;
  wire [7:7] pull_resistor_2_node;
  wire [15:0] register_1_q;

  Register_part #(.width(16)) register_1 (
    .D({rom_1_data_2, rom_1_data}), .en(controlunit_1_enable_ir), .Q(register_1_q), .clk(CLK), .clr(in_1));
  or or_1 (RAM_IO, ST, LD);
  ControlUnit controlunit_1 (
    .IW(register_1_q), .ALU_CMD(controlunit_1_alu_cmd), .enable_input(controlunit_1_enable_input),
    .writeRegselect(controlunit_1_writeregselect), .enable_Port_A(controlunit_1_enable_port_a),
    .Port_A_select(controlunit_1_port_a_select), .enable_Port_B(controlunit_1_enable_port_b),
    .Port_B_select(controlunit_1_port_b_select), .Increment_PC(controlunit_1_increment_pc),
    .Enable_IR(controlunit_1_enable_ir), .Reset(in_1), .CLK(CLK), .IW_8___15(RelJ), .ALU_Flags(Flags),
    .Bus_Buffer_ALU(controlunit_1_bus_buffer_alu), .Bus_Buffer_IW(controlunit_1_bus_buffer_iw),
    .Bus_Register_Feedback(controlunit_1_bus_register_feedback), .RAM_store_enable(ST), .RAM_load_enable(LD),
    .ROM_load_enable(controlunit_1_rom_load_enable), .Exe(Exe), .RomL_H(controlunit_1_roml_h),
    .CalculateRelativeJump(RelConst), .write(write));
  Multiplexer #(.width(8), .enable("false")) multiplexer_1 (
    .in0(rom_1_data), .in1(rom_1_data_2), .out(multiplexer_1_out), .sel(controlunit_1_roml_h));
  assign controlled_buffer_1_out = controlunit_1_rom_load_enable ? multiplexer_1_out : 8'bz;  // Controlled_Buffer controlled_buffer_1
  assign controlled_buffer_1_out = controlunit_1_bus_buffer_iw ? RelJ : 8'bz;  // Controlled_Buffer controlled_buffer_2
  assign controlled_buffer_1_out = controlunit_1_bus_buffer_alu ? alu_1_res : 8'bz;  // Controlled_Buffer controlled_buffer_3
  and and_1 (and_1_out, RAM_IO, Mem);
  Multiplexer #(.width(8), .enable("false")) multiplexer_2 (
    .in0(register_2_pc), .in1(RomAddr), .out(multiplexer_2_out), .sel(controlunit_1_rom_load_enable));
  Register register_2 (
    .Increment_PC(controlunit_1_increment_pc), .enable_input(controlunit_1_enable_input),
    .WriteRegisterSelect(controlunit_1_writeregselect), .Port_Input(controlled_buffer_1_out), .CLK(CLK),
    .PC(register_2_pc), .Port_A(RomAddr), .enable_Port_A(controlunit_1_enable_port_a),
    .Port_A_select(controlunit_1_port_a_select), .Port_B({Mem, RamAddr}),
    .enable_Port_B(controlunit_1_enable_port_b), .Port_B_select(controlunit_1_port_b_select), .Reset(in_1));
  assign controlled_buffer_1_out = controlunit_1_bus_register_feedback ? RomAddr : 8'bz;  // Controlled_Buffer controlled_buffer_4
  // Probe on controlunit_1_alu_cmd
  RAM #(.addrWidth(7), .bus("separate")) ram_1 (
    .addr(RamAddr), .din(controlled_buffer_1_out), .data(controlled_buffer_1_out), .str(ST), .sel(and_1_out),
    .clk(CLK), .ld(LD));  // open: clr
  ROM #(.dataWidth(16)) rom_1 (.addr(multiplexer_2_out), .data({rom_1_data_2, rom_1_data}));  // open: sel
  Hex_Digit_Display hex_digit_display_1 (.value(RomAddr[7:4]));  // open: dp
  Hex_Digit_Display hex_digit_display_2 (.value(RomAddr[3:0]));  // open: dp
  ALU alu_1 (
    .Res(alu_1_res), .Cmd(controlunit_1_alu_cmd), .Opt1(RomAddr), .Opt2(multiplexer_3_out),
    .to_flag_register(Flags));
  Hex_Digit_Display hex_digit_display_3 (.value({Mem, RamAddr[6:4]}));  // open: dp
  Hex_Digit_Display hex_digit_display_4 (.value(RamAddr[3:0]));  // open: dp
  Multiplexer #(.width(8), .enable("false")) multiplexer_3 (
    .in0({Mem, RamAddr}), .in1(RelJ), .out(multiplexer_3_out), .sel(RelConst));
  // Probe on Flags
  Hex_Digit_Display hex_digit_display_5 (.value(alu_1_res[7:4]));  // open: dp
  Hex_Digit_Display hex_digit_display_6 (.value(alu_1_res[3:0]));  // open: dp
  TTY tty_1 (.data(controlled_buffer_1_out[6:0]), .clk(CLK), .we(decoder_1_out0), .clr(decoder_1_out6));
  Keyboard #(.buflen(16)) keyboard_1 (
    .clk(and_2_out), .clr(decoder_1_out2), .avail(keyboard_1_avail[0]), .data(keyboard_1_data));  // open: re
  and and_2 (and_2_out, write, decoder_1_out3);
  Pull_Resistor #(.pull(1)) pull_resistor_1 (.node(Mem));
  Decoder #(.select(3), .disabled(0)) decoder_1 (
    .out0(decoder_1_out0), .out1(decoder_1_out1), .out2(decoder_1_out2), .out3(decoder_1_out3),
    .out4(decoder_1_out4), .out6(decoder_1_out6), .sel(RamAddr[2:0]), .en(and_3_out));  // open: out5, out7
  and and_3 (and_3_out, RAM_IO, ~Mem);  // AND_Gate
  Clock clock_1 (.out(CLK));
  assign controlled_buffer_1_out = decoder_1_out1 ? {{7{1'b0}}, keyboard_1_avail[0]} : 8'bz;  // Controlled_Buffer controlled_buffer_5
  assign controlled_buffer_1_out = decoder_1_out3 ? {1'b0, keyboard_1_data} : 8'bz;  // Controlled_Buffer controlled_buffer_6
  Random #(.width(7)) random_1 (.clk(CLK), .out(random_1_out));  // open: next, clr
  Pull_Resistor pull_resistor_2 (.node(pull_resistor_2_node[7]));
  assign controlled_buffer_1_out = decoder_1_out4 ? {pull_resistor_2_node[7], random_1_out} : 8'bz;  // Controlled_Buffer controlled_buffer_7

  // Other names for the same wires on the sheet: Reset = in_1

  // Notes on the sheet:
  //   contents of rom_1 (hex, n*v repeats v):
  //   441 509 8041 4408 42 c041 cb43 280c 280d 4f2 6475 fc55 8045 141 47 509 2875 fe55 16f2 343 e09 9408
  //   9c08 a46 9875 f655 a0c8 8142 2971 43c8 143 2cf1 443 4c75 3457 589 2f44 8c75 3057 3a44 7075 2c57 4f3
  //   973 143 4c75 f557 44 f42 16f3 1489 28f8 2cf4 5652 79f4 3270 5652 1ff3 f755 16f3 1709 9875 4050 4b51
  //   42 cc41 d243 280c 280d 4f2 6475 fc55 41 42 50 42 d241 dd43 280c 280d 4f2 6475 fc55 41 42 50 42 dd41
  //   f743 280c 280d 4f2 6475 fc55 41 42 50 95*0 7245 6172 6574 5a20 6861 206c 305b 2e2e 312e 3732 3a5d
  //   200a 6952 6863 6974 2067 293a a20 6146 7473 202c 6c67 6965 6863 6e20 636f 6d68 6c61 a21 283a 5920
  //   756f 2072 4350 7220 6e61 6920 746e 206f 2061 7270 626f 656c 206d 6e61 2064 656e 6465 2073 6f74 7220
  //   7365 6174 7472 a21
  //   0 display
  //   1 Bus char avaiable
  //   2 clear KB
  //   3 Bus ASCII
  //   4 RNG
  //   5 undef.
  //   6 clear display
  //   7 RNG Seed (omitted, no seed needed)
endmodule

module ALU (
  input  [3:0] Cmd,
  input  [7:0] Opt1,
  input  [7:0] Opt2,
  output [7:0] Res,
  output [7:0] to_flag_register
);

  wire addFlow, and_1_out, and_2_out, and_3_out, and_7_out, and_8_out, and_9_out, decNeg, decZero, incFlow,
       mFlow, nor_1_out, or_4_out, subNeg, subZero, testNeg, testZero;
  wire [1:0] pull_resistor_3_node;
  wire [2:0] bitselector_1_out;
  wire [7:0] adder_1_out, adder_2_out, and_10_out, multiplier_1_out, multOverflow, negator_1_out, not_1_out,
       or_3_out, shifter_1_out, shifter_2_out, subtractor_1_out, subtractor_2_out, subtractor_3_out,
       xnor_1_out, xor_1_out;

  Hex_Digit_Display hex_digit_display_1 (.value(Opt1[3:0]));  // open: dp
  Hex_Digit_Display hex_digit_display_2 (.value(Opt1[7:4]));  // open: dp
  Hex_Digit_Display hex_digit_display_3 (.value(Opt2[7:4]));  // open: dp
  Hex_Digit_Display hex_digit_display_4 (.value(Opt2[3:0]));  // open: dp
  and and_1 (and_1_out, addFlow, ~Cmd[3], ~Cmd[2], ~Cmd[1], ~Cmd[0]);  // AND_Gate
  Pull_Resistor pull_resistor_1 (.node(Opt1));
  and and_2 (and_2_out, mFlow, ~Cmd[3], Cmd[2], ~Cmd[1], ~Cmd[0]);  // AND_Gate
  and and_3 (and_3_out, incFlow, ~Cmd[3], ~Cmd[2], Cmd[1], ~Cmd[0]);  // AND_Gate
  Pull_Resistor pull_resistor_2 (.node(Opt2));
  or or_1 (to_flag_register[1], and_1_out, and_3_out, and_2_out);
  and and_4 (testZero, Cmd[0], ~Cmd[1], Cmd[2], ~Cmd[3]);  // AND_Gate
  and and_5 (subZero, Cmd[0], ~Cmd[1], ~Cmd[2], ~Cmd[3]);  // AND_Gate
  and and_6 (decZero, Cmd[0], Cmd[1], ~Cmd[2], ~Cmd[3]);  // AND_Gate
  BitSelector #(.group(3)) bitselector_1 (.in(Opt2), .out(bitselector_1_out), .sel(pull_resistor_3_node));
  Pull_Resistor pull_resistor_3 (.node(pull_resistor_3_node));
  and and_7 (and_7_out, testNeg, testZero);
  and and_8 (and_8_out, subNeg, subZero);
  and and_9 (and_9_out, decNeg, decZero);
  Subtractor subtractor_1 (.a(Opt1), .b(Opt2), .out(subtractor_1_out), .bout(subNeg));  // open: bin
  Subtractor subtractor_2 (.a(Opt1), .b(Opt2), .out(subtractor_2_out), .bout(testNeg));  // open: bin
  or or_2 (to_flag_register[2], and_7_out, and_8_out, and_9_out);
  Adder adder_1 (.a(Opt1), .b(Opt2), .out(adder_1_out), .cout(addFlow));  // open: cin
  Adder adder_2 (.a(8'h1), .b(Opt2), .out(adder_2_out), .cout(incFlow));  // open: cin
  Subtractor subtractor_3 (.a(Opt2), .b(8'h1), .out(subtractor_3_out), .bout(decNeg));  // open: bin
  Multiplier multiplier_1 (.a(Opt1), .b(Opt2), .out(multiplier_1_out), .cout(multOverflow));  // open: cin
  assign and_10_out = Opt1 & Opt2;  // AND_Gate and_10, 8 bits wide
  assign or_3_out = Opt1 | Opt2;  // OR_Gate or_3, 8 bits wide
  assign not_1_out = ~Opt2;  // NOT_Gate not_1, 8 bits wide
  Negator negator_1 (.in(Opt2), .out(negator_1_out));
  assign xor_1_out = Opt1 ^ Opt2;  // XOR_Gate xor_1, 8 bits wide
  assign xnor_1_out = ~(Opt1 ^ Opt2);  // XNOR_Gate xnor_1, 8 bits wide
  Shifter shifter_1 (.in(Opt1), .\dist (bitselector_1_out), .out(shifter_1_out));
  Shifter #(.shift("lr")) shifter_2 (.in(Opt1), .\dist (bitselector_1_out), .out(shifter_2_out));
  Multiplexer #(.select(4), .width(8), .disabled(0), .enable("false")) multiplexer_1 (
    .in0(adder_1_out), .in1(subtractor_1_out), .in2(adder_2_out), .in3(subtractor_3_out),
    .in4(multiplier_1_out), .in5(subtractor_2_out), .in8(and_10_out), .in9(or_3_out), .in10(not_1_out),
    .in11(negator_1_out), .in12(xor_1_out), .in13(xnor_1_out), .in14(shifter_1_out), .in15(shifter_2_out),
    .out(Res), .sel(Cmd));  // open: in6, in7
  nor nor_1 (nor_1_out, Res[7], Res[6], Res[5], Res[4], Res[3], Res[2], Res[1], Res[0]);
  and and_11 (to_flag_register[0], nor_1_out, or_4_out);
  or or_4 (or_4_out, testZero, subZero, decZero);
  or or_5 (mFlow, multOverflow[7], multOverflow[6], multOverflow[5], multOverflow[4], multOverflow[3], multOverflow[2], multOverflow[1], multOverflow[0]);
  Hex_Digit_Display hex_digit_display_5 (.value(Res[3:0]));  // open: dp
  Hex_Digit_Display hex_digit_display_6 (.value(Res[7:4]));  // open: dp

  assign to_flag_register[7:3] = {5{1'b0}};

  // Other names for the same wires on the sheet: Carry = to_flag_register[1]; Negative = to_flag_register[2]

  // Notes on the sheet:
  //   CMD in Hex
  //   0 Add
  //   1 Sub
  //   2 INC
  //   3 DEC
  //   4 MULT
  //   5 TEST
  //   8 AND
  //   9 OR
  //   A NOT
  //   B Neg
  //   C XOR
  //   D XNOR
  //   E SHL
  //   F SHR
  //   negieren= bitwise not und + 1
  //   is zero
endmodule

module ControlUnit (
  input  Reset,
  input  CLK,
  input  [15:0] IW,
  input  [7:0] ALU_Flags,
  output [3:0] ALU_CMD,
  output write,
  output enable_input,
  output [2:0] writeRegselect,
  output enable_Port_A,
  output [2:0] Port_A_select,
  output enable_Port_B,
  output [2:0] Port_B_select,
  output Increment_PC,
  output Enable_IR,
  output Bus_Buffer_IW,
  output Bus_Buffer_ALU,
  output Bus_Register_Feedback,
  output RAM_store_enable,
  output RAM_load_enable,
  output ROM_load_enable,
  output Exe,
  output RomL_H,
  output CalculateRelativeJump,
  output [7:0] IW_8___15
);

  wire ALU, and_1_out, constant_addr, decode, decoder_2_out0, decoder_2_out1, decoder_2_out2, decoder_2_out3,
       decoder_2_out4, decoder_2_out5, decoder_2_out6, decoder_2_out7, fetch, JC_out, JMP_out, JNC_out,
       JNNR_out, JNR_out, JNZ_out, JNZR_out, JZ_out, JZR_out, LDI, Memory_out, MOVE, not_1_out, or_1_out;
  wire [1:0] Cycle;
  wire [2:0] multiplexer_3_out;
  wire [7:0] demultiplexer_1_out0, demultiplexer_1_out1, register_1_q, subtractor_1_out;
  wire [9:9] or_2_out;
  wire [10:0] rom_1_data;

  Decoder #(.select(2), .enable("false")) decoder_1 (
    .out0(fetch), .out1(decode), .out2(Exe), .out3(write), .sel(Cycle));
  Counter #(.width(2), .max('h3)) counter_1 (.Q(Cycle), .clk(CLK), .clr(Reset));  // open: load, D, count, carry
  and JMP (JMP_out, IW[4], ~IW[5], IW[6]);  // AND_Gate
  Decoder #(.select(3), .disabled(0)) decoder_2 (
    .out0(decoder_2_out0), .out1(decoder_2_out1), .out2(decoder_2_out2), .out3(decoder_2_out3),
    .out4(decoder_2_out4), .out5(decoder_2_out5), .out6(decoder_2_out6), .out7(decoder_2_out7),
    .sel(IW[2:0]), .en(JMP_out));
  and and_1 (and_1_out, ALU, Exe);
  Register_part register_1 (.D(ALU_Flags), .en(and_1_out), .Q(register_1_q), .clk(CLK));  // open: clr
  Demultiplexer #(.width(8), .enable("false")) demultiplexer_1 (
    .out0(demultiplexer_1_out0), .out1(demultiplexer_1_out1), .in(IW[15:8]), .sel(CalculateRelativeJump));
  and u_LDI (LDI, ~IW[4], ~IW[5], IW[6]);  // AND_Gate
  and u_ALU (ALU, IW[4], IW[5], IW[6]);
  and Memory (Memory_out, IW[3], ~IW[4], ~IW[5], ~IW[6]);  // AND_Gate
  and JZ (JZ_out, decoder_2_out0, register_1_q[0]);
  and JNZ (JNZ_out, decoder_2_out1, ~register_1_q[0]);  // AND_Gate
  and JC (JC_out, decoder_2_out2, register_1_q[1]);
  and JNC (JNC_out, decoder_2_out3, ~register_1_q[1]);  // AND_Gate
  and JZR (JZR_out, decoder_2_out4, register_1_q[0]);
  and JNZR (JNZR_out, decoder_2_out5, ~register_1_q[0]);  // AND_Gate
  and JNR (JNR_out, decoder_2_out6, register_1_q[2]);
  and JNNR (JNNR_out, decoder_2_out7, ~register_1_q[2]);  // AND_Gate
  or or_1 (or_1_out, ALU, MOVE, Memory_out);
  and u_RomL_H (RomL_H, IW[0], Memory_out);
  or or_2 (or_2_out[9], JZ_out, JNZ_out, JC_out, JNC_out, JZR_out, JNZR_out, JNR_out, JNNR_out);
  or or_3 (CalculateRelativeJump, JNNR_out, JZR_out, JNZR_out, JNR_out);
  Subtractor subtractor_1 (.a(demultiplexer_1_out1), .b(8'h1), .out(subtractor_1_out));  // open: bin, bout
  and and_2 (constant_addr, ~fetch, ~write, or_1_out);  // AND_Gate
  Multiplexer #(.width(4), .enable("false")) multiplexer_1 (
    .in0(IW[3:0]), .in1(4'b0000), .out(ALU_CMD), .sel(CalculateRelativeJump));
  ROM #(.addrWidth(10), .dataWidth(20)) rom_1 (
    .addr({or_2_out[9], IW[6:0], Cycle}),
    .data({ROM_load_enable, RAM_load_enable, RAM_store_enable, Bus_Register_Feedback, Bus_Buffer_ALU, Bus_Buffer_IW, Enable_IR, Increment_PC, enable_Port_B, rom_1_data[10:8], enable_Port_A, rom_1_data[6:4], enable_input, rom_1_data[2:0]}));  // open: sel
  Multiplexer #(.width(8), .enable("false")) multiplexer_2 (
    .in0(demultiplexer_1_out0), .in1(subtractor_1_out), .out(IW_8___15), .sel(CalculateRelativeJump));
  not not_1 (not_1_out, LDI);
  and and_3 (MOVE, ALU_CMD[3], LDI);
  Multiplexer #(.width(3), .enable("false")) multiplexer_3 (
    .in0(ALU_CMD[2:0]), .in1(rom_1_data[2:0]), .out(multiplexer_3_out), .sel(not_1_out));
  Multiplexer #(.width(3), .enable("false")) multiplexer_4 (
    .in0(multiplexer_3_out), .in1(IW[9:7]), .out(writeRegselect), .sel(constant_addr));
  Multiplexer #(.width(3), .enable("false")) multiplexer_5 (
    .in0(rom_1_data[6:4]), .in1(IW[15:13]), .out(Port_A_select), .sel(constant_addr));
  Multiplexer #(.width(3), .enable("false")) multiplexer_6 (
    .in0(rom_1_data[10:8]), .in1(IW[12:10]), .out(Port_B_select), .sel(constant_addr));

  // Other names for the same wires on the sheet: execute = Exe; R3[2:0] = IW[9:7]; R2[2:0] = IW[12:10];
  //   R1[2:0] = IW[15:13]; RelAdd = CalculateRelativeJump

  // Notes on the sheet:
  //   !(a!=b)
  //   !(a==b)
  //   bit 0: isZero
  //   bit 1: Carry
  //   bit 2: Negative
  //   PC+1-1 Jump Compensation
  //   contents of rom_1 (hex, n*v repeats v):
  //   3000 31*0 3000 0 30880 0 3000 0 40808 0 3000 0 80088 0 3000 0 80088 0 3000 0 e0880 0 3000 0 e0880
  //   201*0 3000 0 4008 0 3000 0 4008 0 3000 0 4008 0 3000 0 4008 0 3000 0 4008 0 3000 0 4008 0 3000 0
  //   4008 0 3000 0 4008 0 3000 0 10088 29*0 3000 0 0 0 3000 0 0 0 3000 0 0 0 3000 0 0 0 3000 0 0 0 3000 0
  //   0 0 3000 0 0 0 3000 99*0 3000 0 8888 0 3000 0 8888 0 3000 0 8808 0 3000 0 8808 0 3000 0 8888 0 3000
  //   0 880 9*0 3000 0 8888 0 3000 0 8888 0 3000 0 8888 0 3000 0 8888 0 3000 0 8888 5*0 3000 0 8888 0 3000
  //   0 8888 321*0 3000 0 4008 0 3000 0 4008 0 3000 0 4008 0 3000 0 4008 0 3000 0 8088 0 3000 0 8088 0
  //   3000 0 8088 0 3000 0 8088
endmodule

module TestALU (
  input  Reset,
  output Result_OK,
  output Flags_OK,
  output _0_Failed
);

  wire and_1_out, and_5_out, clock_1_out, comparator_1_eq, multiplexer_1_out, not_1_out;
  wire [3:0] counter_1_q, counter_1_q_2, rom_2_data;
  wire [7:0] alu_1_res, alu_1_to_flag_register, xnor_1_out, xnor_2_out;
  wire [15:0] rom_1_data, rom_3_data;

  Hex_Digit_Display hex_digit_display_1 (.value(counter_1_q_2));  // open: dp
  Clock clock_1 (.out(clock_1_out));
  Hex_Digit_Display hex_digit_display_2 (.value(counter_1_q));  // open: dp
  Multiplexer #(.enable("false")) multiplexer_1 (
    .in0(1'b1), .in1(clock_1_out), .out(multiplexer_1_out), .sel(and_1_out));
  ROM #(.dataWidth(16)) rom_1 (.addr({counter_1_q_2, counter_1_q}), .data(rom_1_data));  // open: sel
  ROM #(.dataWidth(4)) rom_2 (.addr({counter_1_q_2, counter_1_q}), .data(rom_2_data));  // open: sel
  ROM #(.dataWidth(16)) rom_3 (.addr({counter_1_q_2, counter_1_q}), .data(rom_3_data));  // open: sel
  // Probe on {counter_1_q_2, counter_1_q}
  Counter counter_1 (
    .Q({counter_1_q_2, counter_1_q}), .clk(multiplexer_1_out), .clr(Reset));  // open: load, D, count, carry
  and and_1 (and_1_out, not_1_out, and_5_out);
  Hex_Digit_Display hex_digit_display_3 (.value(rom_1_data[11:8]));  // open: dp
  Hex_Digit_Display hex_digit_display_4 (.value(rom_1_data[15:12]));  // open: dp
  Comparator comparator_1 (.a({counter_1_q_2, counter_1_q}), .b({8{1'b1}}), .eq(comparator_1_eq));  // open: gt, lt
  Hex_Digit_Display hex_digit_display_5 (.value(rom_1_data[7:4]));  // open: dp
  ALU alu_1 (
    .Res(alu_1_res), .Cmd(rom_2_data), .Opt1(rom_1_data[15:8]), .Opt2(rom_1_data[7:0]),
    .to_flag_register(alu_1_to_flag_register));
  not not_1 (not_1_out, comparator_1_eq);
  Hex_Digit_Display hex_digit_display_6 (.value(rom_1_data[3:0]));  // open: dp
  // Probe on alu_1_res
  // Probe on rom_3_data[15:8]
  and and_2 (_0_Failed, comparator_1_eq, and_5_out);
  assign xnor_1_out = ~(alu_1_res ^ rom_3_data[7:0]);  // XNOR_Gate xnor_1, 8 bits wide
  assign xnor_2_out = ~(alu_1_to_flag_register ^ rom_3_data[15:8]);  // XNOR_Gate xnor_2, 8 bits wide
  and and_3 (Result_OK, xnor_1_out[0], xnor_1_out[1], xnor_1_out[2], xnor_1_out[3], xnor_1_out[4], xnor_1_out[5], xnor_1_out[6], xnor_1_out[7]);
  and and_4 (Flags_OK, xnor_2_out[0], xnor_2_out[1], xnor_2_out[2], xnor_2_out[3], xnor_2_out[4], xnor_2_out[5], xnor_2_out[6], xnor_2_out[7]);
  and and_5 (and_5_out, Result_OK, Flags_OK);

  // Notes on the sheet:
  //   Next
  //   Command
  //   Operands
  //   expected Result
  //   contents of rom_1 (hex, n*v repeats v):
  //   53f9 330e 5b24 c80f 1562 9efa 22e5 1172 f3e9 8f62 69a6 af18 7c11 d075 636b c369 e802 f17b 7393 4b58
  //   e3c3 b884 5b3a 7121 8fde e7e9 2ddb aa7e d255 5738 92ca cca6 abb8 ba22 d7ef 4cbe 9605 1b4d 9ea3 42c0
  //   f557 c172 e03b 839e b3c9 6f1a 7832 9256 4999 281f d808 b68 66e7 235e 6b4b 3608 e6be f927 bb4a 2a75
  //   2e15 70c3 50bd a33e f8f9 92b8 19fb 9f30 c977 ba46 7244 63f5 7f97 10cc 62c7 f32 2897 965b 24a6 d214
  //   4039 c32 9363 681 5cd1 bff6 ccd0 8c78 4441 207e a691 bf35 9dc5 60fb 3288 6a81 a2a7 4fe3 fbbf 176e
  //   ca7d 135b d92f 5c07 f339 acda b934 8866 be43 d4b0 b28b 9f8d ea9 fc33 1d06 8b1 6576 3b03 8151 69e3
  //   bbce 2b77 106d d2af a072 192f 7b55 89e0 a311 f39 26a3 2c10 d862 ba14 3c1 f039 9486 25a2 aef9 1c5b
  //   6238 e92e 332f 1da7 5e7 a4d8 4bec 6890 265e 19a9 a7bf 2db7 638c 20f4 4d1c 367c e8fc 4c72 7281 7684
  //   b4e6 ba5b e628 6f25 91c4 645 e348 aeee ddf7 52e0 5ef0 5e20 1d25 91c8 cda9 4933 554e 841a 7ddc f5a3
  //   f33e 9290 b3e0 e871 ed61 2d7b aa90 4660 6f9b d57e 6a6 3d53 b74 451f 7886 5cea bb2a f8eb a282 fc06
  //   28f4 69a4 c0a1 2968 89df bef9 bf1b b6d1 bddf 44d5 b2a2 3232 971b 941 ada2 d114 4aa4 222a 5f7c bb94
  //   1735 287f 3d73 e12a 2f7d 3e71 bc9f 204b 28ac 703d fe23 dd0b b53c f1f7 83e2 d623 3cc5 aae9 c8bc adf2
  //   f22 2e17 5b99 d5d0 7a89 3484 47c8 eae5 653d 1869 d58d 2f23
  //   contents of rom_2 (hex, n*v repeats v):
  //   28*0 28*1 28*5 28*8 28*9 28*b 28*c 28*e 28*f
  //   contents of rom_3 (hex, n*v repeats v):
  //   24c 41 7f d7 77 298 207 83 2dc f1 20f c7 8d 245 ce 22c ea 26c 206 a3 2a6 23c 95 92 26d 2d0 208 228
  //   7d 1f 4c8 26 4f3 98 4e8 48e 91 4ce 4fb 482 9e 4f a5 4e5 4ea 55 46 3c 4b0 9 d0 4a3 47f 4c5 20 2e 28
  //   d2 71 4b5 19 4ad 493 65 4ff 4da 41e 6f 52 74 2e 46e 4e8 444 49b 4dd 491 3b 47e be 7 4da 30 485 50 b6
  //   c0 8 40 20 80 35 85 60 0 0 a2 43 bb 6 48 13 9 4 31 88 30 0 2 90 82 8d af ff 1f b9 77 3b d1 eb ff 7f
  //   7d ff f2 3f 7f e9 b3 3f a7 3c fa be c3 f9 96 a7 ff 5f 9e 17 cd e3 fb 5c b5 98 da e7 59 d3 9d e0 b3
  //   ca 18 b4 8e 8a 4c 46 1a 91 6f fa 1d 52 2a b2 ae 7e 38 59 64 7a 1b 9e a1 56 cd 2 53 99 8c 56 3a 26 f4
  //   ab a0 6e 7f 5a fe b6 ec c0 88 0 80 90 80 29 80 7c f8 6c 80 80 c8 c8 b8 12 b4 10 a0 88 f0 b0 e0 0 e8
  //   84 1 1f 1 4 2 3 1f 1b b 1 20 1a 1 55 c 2b 3 0 2d d5 3d 3 47 7 3 c 6 5
  //   1 Success
endmodule

module Register (
  input  Increment_PC,
  input  enable_Port_A,
  input  enable_input,
  input  [2:0] Port_A_select,
  input  [2:0] WriteRegisterSelect,
  input  enable_Port_B,
  input  [2:0] Port_B_select,
  input  [7:0] Port_Input,
  input  CLK,
  input  Reset,
  output [7:0] PC,
  output [7:0] Port_A,
  output [7:0] Port_B
);

  wire decoder_1_out0, decoder_1_out1, decoder_1_out2, decoder_1_out3, decoder_1_out4, decoder_1_out5,
       decoder_1_out6, decoder_1_out7, not_1_out, or_1_out;
  wire [7:0] adder_1_out, multiplexer_1_out, RA_q, RB_q, RC_q, RD_q, RE_q, RF_q, RG_q;

  Decoder #(.select(3), .disabled(0)) decoder_1 (
    .out0(decoder_1_out0), .out1(decoder_1_out1), .out2(decoder_1_out2), .out3(decoder_1_out3),
    .out4(decoder_1_out4), .out5(decoder_1_out5), .out6(decoder_1_out6), .out7(decoder_1_out7),
    .sel(WriteRegisterSelect), .en(enable_input));
  Adder adder_1 (.a(PC), .b(8'h1), .out(adder_1_out));  // open: cin, cout
  not not_1 (not_1_out, Increment_PC);
  or or_1 (or_1_out, Increment_PC, decoder_1_out0);
  Multiplexer #(.width(8), .enable("false")) multiplexer_1 (
    .in0(adder_1_out), .in1(Port_Input), .out(multiplexer_1_out), .sel(not_1_out));
  // Probe on multiplexer_1_out
  Register_part u_PC (.D(multiplexer_1_out), .en(or_1_out), .Q(PC), .clk(CLK), .clr(Reset));
  Register_part RA (.D(Port_Input), .en(decoder_1_out1), .Q(RA_q), .clk(CLK), .clr(Reset));
  Register_part RB (.D(Port_Input), .en(decoder_1_out2), .Q(RB_q), .clk(CLK), .clr(Reset));
  Register_part RC (.D(Port_Input), .en(decoder_1_out3), .Q(RC_q), .clk(CLK), .clr(Reset));
  Register_part RD (.D(Port_Input), .en(decoder_1_out4), .Q(RD_q), .clk(CLK), .clr(Reset));
  Register_part RE (.D(Port_Input), .en(decoder_1_out5), .Q(RE_q), .clk(CLK), .clr(Reset));
  Register_part RF (.D(Port_Input), .en(decoder_1_out6), .Q(RF_q), .clk(CLK), .clr(Reset));
  Register_part RG (.D(Port_Input), .en(decoder_1_out7), .Q(RG_q), .clk(CLK), .clr(Reset));
  // Probe on PC
  Multiplexer #(.select(3), .width(8)) multiplexer_2 (
    .in0(PC), .in1(RA_q), .in2(RB_q), .in3(RC_q), .in4(RD_q), .in5(RE_q), .in6(RF_q), .in7(RG_q),
    .out(Port_A), .sel(Port_A_select), .en(enable_Port_A));
  Multiplexer #(.select(3), .width(8)) multiplexer_3 (
    .in0(PC), .in1(RA_q), .in2(RB_q), .in3(RC_q), .in4(RD_q), .in5(RE_q), .in6(RF_q), .in7(RG_q),
    .out(Port_B), .sel(Port_B_select), .en(enable_Port_B));
endmodule
